// Logisim project Ckt_Pin-out.circ as structural Verilog: 14 circuits, main circuit main
module main (
  input  in_1,
  input  Door_Closed,
  input  [3:0] Original_Password,
  input  in_4,
  input  X3,
  input  X2,
  input  Door_closed_2,
  input  X1,
  input  in_9,
  input  X0,
  input  in_11,
  input  in_12,
  input  Change_Password,
  input  A3,
  input  A2,
  input  A1,
  input  A0,
  input  in_18,
  input  X3_2,
  input  X2_2,
  input  X1_2,
  input  X0_2,
  input  Unlock_Button_Inside_the_Car,
  input  ENTER_Button,
  input  Change_Password_2,
  input  Factory_Reset,
  input  in_27,
  output Locked,
  output Unlocked,
  output locked_2,
  output unlocked_2,
  output Alarm
);

  wire _2_1_Mux__4__y1, _2_1_Mux__7__y2, _2_1_Mux__9__y3, _2_1_Mux__12__y4, _2_4_Decoder__5__1y1,
       _2_4_Decoder__7__1y3, _4_1_Mux__7__y1, _4_1_Mux__9__y2, _4_bit_counter_2__13__q1,
       _4_bit_counter_2__14__q0, _4_bit_counter_3__13__q1, _4_bit_counter__11__o3, _4_bit_counter__12__q2,
       _4_bit_counter__13__q1, _4_bit_counter__14__q0, _4_bit_register_2__1q, _4_bit_register_2__2q,
       _4_bit_register_2__3q, _4_bit_register_2__4q, _4_bit_register__1q, _4_bit_register__2q,
       _4_bit_register__3q, _4_bit_register__4q, and_1_out, and_2_out, and_3_out, and_4_out, clock_1_out,
       CLOCK_2_out, Comparator_2_a_bout_2, controlled_buffer_1_out, decoder_1_out1, decoder_1_out3,
       Dual_1_bit__FF__5__q1, Dual_1_bit__FF__6__nq1, Dual_1_bit__FF__9__q2, Factory_Reset_out,
       Hex_Invertors_2__4__2y, Hex_Invertors_2__6__3y, Hex_Invertors_2__8__4y, Hex_Invertors_2__10__5y,
       Hex_Invertors_2__12__6y, Hex_Invertors__2__1y, Hex_Invertors__6__3y, Hex_Invertors__8__4y,
       Hex_Invertors__10__5y, Hex_Invertors__12__6y, LED_Display_Ckt_a, LED_Display_Ckt_b, LED_Display_Ckt_d,
       LED_Display_Ckt_e, LED_Display_Ckt_f, LED_Display_Ckt_g, n74153_1__7__y1, n74153_1__9__y2,
       n74153_2__7__y1, n74153_2__9__y2, not_1_out, not_2_out, not_3_out, not_4_out, not_5_out, not_6_out,
       or_1_out, or_2_out, or_3_out, or_4_out, or_5_out, Quad_4_i_p_AND_2__3__1y, Quad_4_i_p_AND_2__6__2y,
       Quad_4_i_p_AND_2__11__4y, Quad_4_i_p_AND_3__3__1y, Quad_4_i_p_AND_3__6__2y, Quad_4_i_p_AND__3__1y,
       Quad_4_i_p_AND__6__2y, Quad_4_i_p_AND__11__4y, Quad_4_i_p_OR_2__3__1y, Quad_4_i_p_OR_2__6__2y,
       Quad_4_i_p_OR_2__11__4y, Quad_4_i_p_OR__3__1y, Quad_4_i_p_OR__6__2y, Quad_4_i_p_OR__8__3y,
       register_1_q, register_2_q, SN74LVC1G125_y, Unlock_Button__inside_the_car_out;
  wire [1:0] counter_3_q, not_7_out;
  wire [2:1] and_5_out;
  wire [3:0] counter_1_q, counter_2_q, multiplexer_1_out, Password_2_q, Password_q;

  Button ENTER (.out(not_7_out[1]));
  not not_1 (not_1_out, counter_2_q[2]);
  Register #(.width(4)) Password (
    .D({X3, X2, X1, X0}), .en(not_1_out), .Q(Password_q), .clk(not_7_out[1]));  // open: clr
  or or_1 (or_1_out, Change_Password, not_2_out);
  Register #(.width(1)) register_1 (
    .D(Change_Password), .en(in_18), .Q(register_1_q), .clk(and_1_out), .clr(Factory_Reset_out));
  and and_1 (and_1_out, Change_Password, not_3_out, register_2_q);
  Comparator #(.width(4), .mode("unsigned")) comparator_1 (
    .a(Password_q), .b(Password_2_q), .eq(and_5_out[2]));  // open: gt, lt
  Multiplexer #(.width(4)) multiplexer_1 (
    .in0(Original_Password), .in1({X3, X2, X1, X0}), .out(multiplexer_1_out), .sel(register_1_q),
    .en(or_1_out));
  Register #(.width(4)) Password_2 (.D(multiplexer_1_out), .en(in_12), .Q(Password_2_q), .clk(or_2_out));  // open: clr
  or or_2 (or_2_out, not_7_out[1], Factory_Reset_out);
  not not_2 (not_2_out, register_1_q);
  not not_3 (not_3_out, Factory_Reset_out);
  and and_2 (and_2_out, and_5_out[2], not_1_out);
  Register #(.width(1)) register_2 (
    .D(and_5_out[2]), .en(Change_Password), .Q(register_2_q), .clk(and_3_out), .clr(or_3_out));
  or or_3 (or_3_out, not_4_out, Factory_Reset_out);
  not not_4 (not_4_out, Change_Password);
  and and_3 (and_3_out, and_5_out[2], not_7_out[1]);
  Clock clock_1 (.out(clock_1_out));
  and and_4 (and_4_out, clock_1_out, Door_Closed, and_5_out[2]);
  not not_5 (not_5_out, Door_Closed);
  not not_6 (not_6_out, and_5_out[2]);
  assign controlled_buffer_1_out = decoder_1_out3 ? not_6_out : 1'bz;  // Controlled_Buffer controlled_buffer_1
  or or_4 (or_4_out, and_2_out, Factory_Reset_out);
  Decoder #(.select(2), .enable("false")) decoder_1 (
    .out1(decoder_1_out1), .out3(decoder_1_out3), .sel(not_7_out));  // open: out0, out2
  Counter #(.width(4), .max('hf), .ongoal("stay")) counter_1 (
    .load(in_1), .count(1'b1), .Q(counter_1_q), .clk(and_4_out), .clr(or_5_out));  // open: D, carry
  or or_5 (or_5_out, Factory_Reset_out, not_5_out, Unlock_Button__inside_the_car_out);
  Counter #(.width(4), .max('hf)) counter_2 (
    .load(in_4), .count(controlled_buffer_1_out), .Q(counter_2_q), .clk(decoder_1_out1), .clr(or_4_out));  // open: D, carry
  and and_5 (and_5_out[1], counter_1_q[0], counter_1_q[1], counter_1_q[2], counter_1_q[3]);
  not not_7 (not_7_out[0], counter_2_q[2]);
  Counter #(.width(2), .max('h3)) counter_3 (
    .load(in_9), .count(in_11), .Q(counter_3_q), .clk(Factory_Reset_out), .clr(counter_3_q[1]));  // open: D, carry
  Multiplexer #(.select(3)) multiplexer_2 (
    .in0(1'b1), .in1(1'b0), .in2(1'b1), .in3(1'b0), .in4(counter_2_q[2]), .in5(1'b0), .in6(1'b1), .in7(1'b0),
    .out(locked_2), .sel({and_5_out, counter_3_q[1]}));  // open: en
  not not_8 (unlocked_2, locked_2);
  LED u_Alarm (.in(counter_2_q[2]));
  LED_Display LED_Display_Ckt (
    .Input(counter_2_q[2:0]), .a(LED_Display_Ckt_a), .b(LED_Display_Ckt_b), .d(LED_Display_Ckt_d),
    .e(LED_Display_Ckt_e), .f(LED_Display_Ckt_f), .g(LED_Display_Ckt_g));
  Button Unlock_Button__inside_the_car (.out(Unlock_Button__inside_the_car_out));
  Button u_Factory_Reset (.out(Factory_Reset_out));
  _7_Segment_Display u_7_segment_display_1 (
    .g(LED_Display_Ckt_g), .f(LED_Display_Ckt_a), .a(LED_Display_Ckt_b), .b(1'b1), .e(LED_Display_Ckt_f),
    .d(LED_Display_Ckt_e), .c(LED_Display_Ckt_d));  // open: dp
  Clock CLOCK_2 (.out(CLOCK_2_out));
  _7404 Hex_Invertors (
    ._1__1A(Factory_Reset), ._2__1Y(Hex_Invertors__2__1y), ._5__3A(Alarm), ._6__3Y(Hex_Invertors__6__3y),
    ._7__GND(1'b0), ._14__Vcc(1'b1), ._13__6A(Change_Password_2), ._12__6Y(Hex_Invertors__12__6y),
    ._11__5A(Quad_4_i_p_OR__3__1y), ._10__5Y(Hex_Invertors__10__5y), ._9__4A(Comparator_2_a_bout_2),
    ._8__4Y(Hex_Invertors__8__4y));  // open: _3__2A, _4__2Y
  _54173 _4_bit_register (
    .M(Alarm), .N(Alarm), ._1Q(_4_bit_register__1q), ._2Q(_4_bit_register__2q), ._3Q(_4_bit_register__3q),
    ._4Q(_4_bit_register__4q), .CLK(ENTER_Button), .GND(1'b0), .Vcc(1'b1), ._1D(X0_2), ._2D(X1_2),
    ._3D(X2_2), ._4D(X3_2), .nG1(ENTER_Button), .nG2(ENTER_Button));  // open: CLR
  _7474 Dual_1_bit__FF (
    ._1__CLR1(Factory_Reset), ._2__D1(Change_Password_2), ._3__CLK1(Quad_4_i_p_AND__6__2y), ._4__PR1(1'b0),
    ._5__Q1(Dual_1_bit__FF__5__q1), ._6__nQ1(Dual_1_bit__FF__6__nq1), ._7__GND(1'b0), ._14__Vcc(1'b1),
    ._13__CLR2(Quad_4_i_p_OR__8__3y), ._12__D2(Comparator_2_a_bout_2), ._11__CLK2(Quad_4_i_p_AND__11__4y),
    ._10__PR2(1'b0), ._9__Q2(Dual_1_bit__FF__9__q2));  // open: _8__nQ2
  _7432 Quad_4_i_p_OR (
    ._1__1A(Change_Password_2), ._2__1B(Dual_1_bit__FF__6__nq1), ._3__1Y(Quad_4_i_p_OR__3__1y),
    ._4__2A(ENTER_Button), ._5__2B(Factory_Reset), ._6__2Y(Quad_4_i_p_OR__6__2y), ._7__GND(1'b0),
    ._14__Vcc(1'b1), ._10__3B(Factory_Reset), ._9__3A(Hex_Invertors__12__6y), ._8__3Y(Quad_4_i_p_OR__8__3y));  // open: _13__4B, _12__4A, _11__4Y
  _7408 Quad_4_i_p_AND (
    ._1__1A(Change_Password_2), ._2__1B(Hex_Invertors__2__1y), ._3__1Y(Quad_4_i_p_AND__3__1y),
    ._4__2A(Quad_4_i_p_AND__3__1y), ._5__2B(Dual_1_bit__FF__9__q2), ._6__2Y(Quad_4_i_p_AND__6__2y),
    ._7__GND(1'b0), ._14__Vcc(1'b1), ._13__4B(Comparator_2_a_bout_2), ._12__4A(ENTER_Button),
    ._11__4Y(Quad_4_i_p_AND__11__4y));  // open: _10__3B, _9__3A, _8__3Y
  _7404 Hex_Invertors_2 (
    ._1__1A(Unlocked), ._2__1Y(Locked), ._3__2A(_4_bit_counter_2__14__q0), ._4__2Y(Hex_Invertors_2__4__2y),
    ._5__3A(Alarm), ._6__3Y(Hex_Invertors_2__6__3y), ._7__GND(1'b0), ._14__Vcc(1'b1),
    ._13__6A(Door_closed_2), ._12__6Y(Hex_Invertors_2__12__6y), ._11__5A(Quad_4_i_p_OR_2__11__4y),
    ._10__5Y(Hex_Invertors_2__10__5y), ._9__4A(_4_bit_counter_3__13__q1), ._8__4Y(Hex_Invertors_2__8__4y));
  _74157 _2_1_Mux (
    ._1__S(Dual_1_bit__FF__5__q1), ._2__A1(A0), ._3__B1(_4_bit_register__1q), ._4__Y1(_2_1_Mux__4__y1),
    ._5__A2(A1), ._6__B2(_4_bit_register__2q), ._7__Y2(_2_1_Mux__7__y2), ._8__GND(1'b0), ._16__Vcc(1'b1),
    ._15__G(Hex_Invertors__10__5y), ._14__A4(A3), ._13__B4(_4_bit_register__4q), ._12__Y4(_2_1_Mux__12__y4),
    ._11__A3(A2), ._10__B3(_4_bit_register__3q), ._9__Y3(_2_1_Mux__9__y3));
  _54173 _4_bit_register_2 (
    .M(1'b0), .N(1'b0), ._1Q(_4_bit_register_2__1q), ._2Q(_4_bit_register_2__2q),
    ._3Q(_4_bit_register_2__3q), ._4Q(_4_bit_register_2__4q), .CLK(Quad_4_i_p_OR__6__2y), .GND(1'b0),
    .Vcc(1'b1), .CLR(Quad_4_i_p_OR__6__2y), ._1D(_2_1_Mux__4__y1), ._2D(_2_1_Mux__7__y2),
    ._3D(_2_1_Mux__9__y3), ._4D(_2_1_Mux__12__y4), .nG1(Quad_4_i_p_OR__6__2y), .nG2(Quad_4_i_p_OR__6__2y));
  _7408 Quad_4_i_p_AND_2 (
    ._1__1A(CLOCK_2_out), ._2__1B(Door_closed_2), ._3__1Y(Quad_4_i_p_AND_2__3__1y),
    ._4__2A(Quad_4_i_p_AND_2__3__1y), ._5__2B(Factory_Reset), ._6__2Y(Quad_4_i_p_AND_2__6__2y),
    ._7__GND(1'b0), ._14__Vcc(1'b1), ._13__4B(Factory_Reset), ._12__4A(Hex_Invertors_2__6__3y),
    ._11__4Y(Quad_4_i_p_AND_2__11__4y));  // open: _10__3B, _9__3A, _8__3Y
  _7485 Comparator_2 (
    .B3(_4_bit_register_2__4q), .A_Bin(1'b0), .A_Bin_2(1'b1), .A_Bin_3(1'b0),
    .A_Bout_2(Comparator_2_a_bout_2), .GND(1'b0), .Vcc(1'b1), .A3(X3_2), .B2(_4_bit_register_2__3q),
    .A2(X2_2), .A1(X1_2), .B1(_4_bit_register_2__2q), .A0(X0_2), .B0(_4_bit_register_2__1q));  // open: A_Bout, A_Bout_3
  _74139 _2_4_Decoder (
    ._1__1G(1'b0), ._2__1A(Hex_Invertors__6__3y), ._3__1B(ENTER_Button), ._5__1Y1(_2_4_Decoder__5__1y1),
    ._7__1Y3(_2_4_Decoder__7__1y3), ._16__Vcc(1'b1), ._8__GND(1'b0));  // open: _4__1Y0, _6__1Y2, _15__2G, _14__2A, _13__2B, _12__2Y0, _11__2Y1, _10__2Y2, _9__2Y3
  _74161 _4_bit_counter (
    ._1__nMR(Quad_4_i_p_OR_2__6__2y), ._2__CP(Quad_4_i_p_AND_2__6__2y), ._7__CEP(1'b1), ._8__GND(1'b0),
    ._16__Vcc(1'b1), ._14__Q0(_4_bit_counter__14__q0), ._13__Q1(_4_bit_counter__13__q1),
    ._12__Q2(_4_bit_counter__12__q2), ._11__O3(_4_bit_counter__11__o3), ._10__CET(1'b1), ._9__nPE(1'b1));  // open: _3__D0, _4__D1, _5__D2, _6__D3, _15__TC
  _7432 Quad_4_i_p_OR_2 (
    ._1__1A(Hex_Invertors_2__12__6y), ._2__1B(Factory_Reset), ._3__1Y(Quad_4_i_p_OR_2__3__1y),
    ._4__2A(Quad_4_i_p_OR_2__3__1y), ._5__2B(Unlock_Button_Inside_the_Car), ._6__2Y(Quad_4_i_p_OR_2__6__2y),
    ._7__GND(1'b0), ._14__Vcc(1'b1), ._13__4B(Hex_Invertors_2__12__6y), ._12__4A(Quad_4_i_p_AND_2__11__4y),
    ._11__4Y(Quad_4_i_p_OR_2__11__4y));  // open: _10__3B, _9__3A, _8__3Y
  Buffer SN74LVC1G125 (
    .OE__prime(_2_4_Decoder__7__1y3), .A(Hex_Invertors__8__4y), .GND(1'b0), .Vcc(1'b1), .Y(SN74LVC1G125_y));
  _7408 Quad_4_i_p_AND_3 (
    ._1__1A(_4_bit_counter__14__q0), ._2__1B(_4_bit_counter__13__q1), ._3__1Y(Quad_4_i_p_AND_3__3__1y),
    ._4__2A(Quad_4_i_p_AND_3__3__1y), ._5__2B(_4_bit_counter__12__q2), ._6__2Y(Quad_4_i_p_AND_3__6__2y),
    ._7__GND(1'b0), ._14__Vcc(1'b1), ._10__3B(Quad_4_i_p_AND_3__6__2y), ._9__3A(_4_bit_counter__11__o3),
    ._8__3Y(Quad_4_i_p_AND_3__6__2y));  // open: _13__4B, _12__4A, _11__4Y
  _74161 _4_bit_counter_2 (
    ._1__nMR(Hex_Invertors_2__10__5y), ._2__CP(_2_4_Decoder__5__1y1), ._7__CEP(SN74LVC1G125_y),
    ._8__GND(1'b0), ._16__Vcc(1'b1), ._14__Q0(_4_bit_counter_2__14__q0), ._13__Q1(_4_bit_counter_2__13__q1),
    ._12__Q2(Alarm), ._10__CET(1'b1), ._9__nPE(1'b1));  // open: _3__D0, _4__D1, _5__D2, _6__D3, _15__TC, _11__O3
  _74161 _4_bit_counter_3 (
    ._1__nMR(Hex_Invertors_2__8__4y), ._2__CP(Factory_Reset), ._7__CEP(1'b1), ._8__GND(1'b0),
    ._16__Vcc(1'b1), ._13__Q1(_4_bit_counter_3__13__q1), ._10__CET(1'b1), ._9__nPE(1'b1));  // open: _3__D0, _4__D1, _5__D2, _6__D3, _15__TC, _14__Q0, _12__Q2, _11__O3
  _74151 _8_1_Mux (
    ._1__D3(1'b0), ._2__D2(1'b1), ._3__D1(1'b0), ._4__D0(1'b1), ._5__Y(Unlocked), ._7__nG(1'b1),
    ._8__GND(1'b0), ._16__Vcc(1'b1), ._15__D4(Alarm), ._14__D5(1'b0), ._13__D6(1'b1), ._12__D7(1'b0),
    ._11__A(_4_bit_counter_3__13__q1), ._10__B(Quad_4_i_p_AND_3__6__2y), ._9__C(Factory_Reset));  // open: _6__W
  _74153 _4_1_Mux (
    ._1__nG1(1'b0), ._2__B(Alarm), ._3__1C3(1'b1), ._4__1C2(1'b1), ._5__1C1(1'b0),
    ._6__1C0(Hex_Invertors_2__4__2y), ._7__Y1(_4_1_Mux__7__y1), ._8__GND(1'b0), ._16__Vcc(1'b1),
    ._15__nG2(1'b0), ._14__A(_4_bit_counter_2__13__q1), ._13__2C3(1'b0), ._12__2C2(Hex_Invertors_2__4__2y),
    ._11__2C1(Hex_Invertors_2__4__2y), ._10__2C0(_4_bit_counter_2__14__q0), ._9__Y2(_4_1_Mux__9__y2));
  _74153 u_74153_1 (
    ._1__nG1(1'b0), ._2__B(Alarm), ._3__1C3(1'b1), ._4__1C2(1'b1), ._5__1C1(_4_bit_counter_2__14__q0),
    ._6__1C0(1'b1), ._7__Y1(n74153_1__7__y1), ._8__GND(1'b0), ._16__Vcc(1'b1), ._15__nG2(1'b0),
    ._14__A(_4_bit_counter_2__13__q1), ._13__2C3(1'b0), ._12__2C2(Hex_Invertors_2__4__2y),
    ._11__2C1(Hex_Invertors_2__4__2y), ._10__2C0(_4_bit_counter_2__14__q0), ._9__Y2(n74153_1__9__y2));
  _74153 u_74153_2 (
    ._1__nG1(1'b0), ._2__B(Alarm), ._3__1C3(_4_bit_counter_2__14__q0), ._4__1C2(Hex_Invertors_2__4__2y),
    ._5__1C1(Hex_Invertors_2__4__2y), ._6__1C0(1'b0), ._7__Y1(n74153_2__7__y1), ._8__GND(1'b0),
    ._16__Vcc(1'b1), ._15__nG2(1'b0), ._14__A(_4_bit_counter_2__13__q1), ._13__2C3(1'b1),
    ._12__2C2(_4_bit_counter_2__14__q0), ._11__2C1(Hex_Invertors_2__4__2y), ._10__2C0(1'b1),
    ._9__Y2(n74153_2__9__y2));

  // Notes on the sheet:
  //   This can be used to reset if user takes it to repair center
  //   a
  //   b
  //   c
  //   d
  //   e
  //   f
  //   g
endmodule

// LED CKT
module LED_Display (
  input  [2:0] Input,
  output a,
  output b,
  output d,
  output e,
  output f,
  output g
);

  wire not_1_out;

  not not_1 (not_1_out, Input[0]);
  Multiplexer #(.select(2)) multiplexer_1 (
    .in0(not_1_out), .in1(1'b0), .in2(1'b1), .in3(1'b1), .out(a), .sel(Input[2:1]));  // open: en
  Multiplexer #(.select(2)) multiplexer_2 (
    .in0(Input[0]), .in1(not_1_out), .in2(not_1_out), .in3(1'b0), .out(b), .sel(Input[2:1]));  // open: en
  Multiplexer #(.select(2)) multiplexer_3 (
    .in0(1'b1), .in1(Input[0]), .in2(1'b1), .in3(1'b1), .out(d), .sel(Input[2:1]));  // open: en
  Multiplexer #(.select(2)) multiplexer_4 (
    .in0(Input[0]), .in1(not_1_out), .in2(not_1_out), .in3(1'b0), .out(e), .sel(Input[2:1]));  // open: en
  Multiplexer #(.select(2)) multiplexer_5 (
    .in0(1'b0), .in1(not_1_out), .in2(not_1_out), .in3(1'b0), .out(f), .sel(Input[2:1]));  // open: en
  Multiplexer #(.select(2)) multiplexer_6 (
    .in0(1'b1), .in1(not_1_out), .in2(Input[0]), .in3(1'b1), .out(g), .sel(Input[2:1]));  // open: en
endmodule

module Buffer (
  input  OE__prime,
  input  Vcc,
  input  A,
  input  GND,
  output Y
);

  wire buffer_1_out, not_1_out;

  not not_1 (not_1_out, OE__prime);
  buf buffer_1 (buffer_1_out, not_1_out);
  assign Y = buffer_1_out ? A : 1'bz;  // Controlled_Buffer controlled_buffer_1
endmodule

module _7485 (
  input  Vcc,
  input  B3,
  input  A_Bin,
  input  A3,
  input  A_Bin_2,
  input  B2,
  input  A_Bin_3,
  input  A2,
  input  A1,
  input  B1,
  input  A0,
  input  B0,
  input  GND,
  output A_Bout,
  output A_Bout_2,
  output A_Bout_3
);

  wire and_1_out, and_2_out, and_3_out, and_4_out, and_5_out, and_6_out, and_7_out, and_8_out, and_9_out,
       and_10_out, and_11_out, and_12_out, and_13_out, and_14_out, and_15_out, and_16_out, and_17_out,
       and_18_out, and_19_out, and_20_out, and_21_out, and_22_out, and_23_out, and_24_out, and_25_out,
       and_26_out, and_27_out, and_28_out, and_29_out, and_30_out, and_31_out, and_32_out, and_33_out,
       and_34_out, and_35_out, and_36_out, and_37_out, and_38_out, and_39_out, and_40_out, not_1_out,
       not_2_out, not_3_out, not_4_out, not_5_out, not_6_out, not_7_out, not_8_out, not_9_out, not_10_out,
       not_11_out, not_12_out, not_13_out, not_14_out, not_15_out, not_16_out, not_17_out, not_18_out,
       not_19_out, not_20_out, not_21_out, not_22_out, not_23_out, not_24_out, not_25_out, not_26_out,
       not_27_out, not_28_out, not_29_out, not_30_out, not_31_out, not_32_out, not_33_out, not_34_out,
       not_35_out, not_36_out, not_37_out, not_38_out, not_39_out, not_40_out, or_1_out, or_2_out, or_3_out,
       or_4_out, or_5_out, or_6_out, or_7_out, or_8_out, or_9_out, or_10_out, or_11_out, or_12_out,
       or_13_out, or_14_out, or_15_out, or_16_out;

  not not_1 (not_1_out, A3);
  not not_2 (not_2_out, B3);
  and and_1 (and_1_out, A3, B3);
  not not_3 (not_3_out, A3);
  and and_2 (and_2_out, not_3_out, not_4_out);
  not not_4 (not_4_out, B3);
  and and_3 (and_3_out, A2, B2);
  not not_5 (not_5_out, A2);
  and and_4 (and_4_out, not_5_out, not_6_out);
  not not_6 (not_6_out, B2);
  and and_5 (and_5_out, A3, B3);
  not not_7 (not_7_out, A3);
  and and_6 (and_6_out, not_7_out, not_8_out);
  not not_8 (not_8_out, B3);
  and and_7 (and_7_out, A2, B2);
  not not_9 (not_9_out, A2);
  and and_8 (and_8_out, not_9_out, not_10_out);
  not not_10 (not_10_out, B2);
  and and_9 (and_9_out, A1, B1);
  not not_11 (not_11_out, A1);
  and and_10 (and_10_out, not_11_out, not_12_out);
  not not_12 (not_12_out, B1);
  not not_13 (not_13_out, A3);
  not not_14 (not_14_out, B3);
  and and_11 (and_11_out, A3, B3);
  not not_15 (not_15_out, A3);
  and and_12 (and_12_out, not_15_out, not_16_out);
  not not_16 (not_16_out, B3);
  and and_13 (and_13_out, A2, B2);
  not not_17 (not_17_out, A2);
  and and_14 (and_14_out, not_17_out, not_18_out);
  not not_18 (not_18_out, B2);
  and and_15 (and_15_out, A3, B3);
  not not_19 (not_19_out, A3);
  and and_16 (and_16_out, not_19_out, not_20_out);
  not not_20 (not_20_out, B3);
  and and_17 (and_17_out, A2, B2);
  not not_21 (not_21_out, A2);
  and and_18 (and_18_out, not_21_out, not_22_out);
  not not_22 (not_22_out, B2);
  and and_19 (and_19_out, A1, B1);
  not not_23 (not_23_out, A1);
  and and_20 (and_20_out, not_23_out, not_24_out);
  not not_24 (not_24_out, B1);
  and and_21 (and_21_out, A3, B3);
  not not_25 (not_25_out, A3);
  and and_22 (and_22_out, not_25_out, not_26_out);
  not not_26 (not_26_out, B3);
  and and_23 (and_23_out, A2, B2);
  not not_27 (not_27_out, A2);
  and and_24 (and_24_out, not_27_out, not_28_out);
  not not_28 (not_28_out, B2);
  and and_25 (and_25_out, A1, B1);
  not not_29 (not_29_out, A1);
  and and_26 (and_26_out, not_29_out, not_30_out);
  not not_30 (not_30_out, B1);
  and and_27 (and_27_out, A0, B0);
  not not_31 (not_31_out, A0);
  and and_28 (and_28_out, not_31_out, not_32_out);
  not not_32 (not_32_out, B0);
  not not_33 (not_33_out, B3);
  not not_34 (not_34_out, B2);
  and and_29 (and_29_out, A3, B3);
  or or_1 (or_1_out, and_29_out, and_30_out);
  and and_30 (and_30_out, not_1_out, not_2_out);
  or or_2 (or_2_out, and_1_out, and_2_out);
  or or_3 (or_3_out, and_3_out, and_4_out);
  not not_35 (not_35_out, B1);
  or or_4 (or_4_out, and_5_out, and_6_out);
  or or_5 (or_5_out, and_7_out, and_8_out);
  or or_6 (or_6_out, and_9_out, and_10_out);
  not not_36 (not_36_out, B0);
  not not_37 (not_37_out, A3);
  not not_38 (not_38_out, A2);
  and and_31 (and_31_out, A3, B3);
  or or_7 (or_7_out, and_31_out, and_32_out);
  and and_32 (and_32_out, not_13_out, not_14_out);
  or or_8 (or_8_out, and_11_out, and_12_out);
  or or_9 (or_9_out, and_13_out, and_14_out);
  not not_39 (not_39_out, A1);
  or or_10 (or_10_out, and_15_out, and_16_out);
  or or_11 (or_11_out, and_17_out, and_18_out);
  or or_12 (or_12_out, and_19_out, and_20_out);
  not not_40 (not_40_out, A0);
  or or_13 (or_13_out, and_21_out, and_22_out);
  or or_14 (or_14_out, and_23_out, and_24_out);
  or or_15 (or_15_out, and_25_out, and_26_out);
  or or_16 (or_16_out, and_27_out, and_28_out);
  and and_33 (and_33_out, A3, not_33_out);
  and and_34 (and_34_out, A2, A_Bin, not_34_out, or_1_out);
  and and_35 (and_35_out, or_2_out, or_3_out, A_Bin_2, A1, not_35_out);
  and and_36 (and_36_out, or_4_out, or_5_out, or_6_out, A0, not_36_out);
  and and_37 (and_37_out, not_37_out, B3);
  and and_38 (and_38_out, not_38_out, A_Bin_3, B2, or_7_out);
  and and_39 (and_39_out, or_8_out, or_9_out, A_Bin_2, not_39_out, B1);
  and and_40 (and_40_out, or_10_out, or_11_out, or_12_out, not_40_out, B0);
  and and_41 (A_Bout_2, or_13_out, or_14_out, A_Bin_2, or_15_out, or_16_out);
  or or_17 (A_Bout, and_33_out, and_34_out, and_35_out, and_36_out);
  or or_18 (A_Bout_3, and_37_out, and_38_out, and_39_out, and_40_out);
endmodule

// SN54173
module _54173 (
  input  M,
  input  Vcc,
  input  N,
  input  CLR,
  input  _1D,
  input  _2D,
  input  _3D,
  input  _4D,
  input  CLK,
  input  nG1,
  input  GND,
  input  nG2,
  output _1Q,
  output _2Q,
  output _3Q,
  output _4Q
);

  wire and_1_out, and_2_out, and_3_out, and_4_out, and_5_out, and_6_out, and_7_out, and_8_out, and_9_out,
       and_10_out, not_1_out, not_2_out, not_3_out, not_4_out, not_5_out, or_1_out, or_2_out, or_3_out,
       or_4_out, s_r_ff_1_q, s_r_ff_2_q, s_r_ff_3_q, s_r_ff_4_q;

  not not_1 (not_1_out, M);
  and and_1 (and_1_out, not_1_out, not_2_out);
  not not_2 (not_2_out, N);
  not not_3 (not_3_out, and_10_out);
  and and_2 (and_2_out, s_r_ff_1_q, and_10_out);
  and and_3 (and_3_out, _1D, not_3_out);
  and and_4 (and_4_out, s_r_ff_2_q, and_10_out);
  and and_5 (and_5_out, _2D, not_3_out);
  and and_6 (and_6_out, s_r_ff_3_q, and_10_out);
  and and_7 (and_7_out, _3D, not_3_out);
  and and_8 (and_8_out, s_r_ff_4_q, and_10_out);
  and and_9 (and_9_out, _4D, not_3_out);
  or or_1 (or_1_out, and_2_out, and_3_out);
  or or_2 (or_2_out, and_4_out, and_5_out);
  or or_3 (or_3_out, and_6_out, and_7_out);
  or or_4 (or_4_out, and_8_out, and_9_out);
  S_R_Flip_Flop s_r_ff_1 (.S(or_1_out), .clk(CLK), .R(CLR), .Q(s_r_ff_1_q));  // open: Qn, preset, reset, en
  S_R_Flip_Flop s_r_ff_2 (.S(or_2_out), .clk(CLK), .R(CLR), .Q(s_r_ff_2_q));  // open: Qn, preset, reset, en
  S_R_Flip_Flop s_r_ff_3 (.S(or_3_out), .clk(CLK), .R(CLR), .Q(s_r_ff_3_q));  // open: Qn, preset, reset, en
  S_R_Flip_Flop s_r_ff_4 (.S(or_4_out), .clk(CLK), .R(CLR), .Q(s_r_ff_4_q));  // open: Qn, preset, reset, en
  assign _1Q = and_1_out ? s_r_ff_1_q : 1'bz;  // Controlled_Buffer controlled_buffer_1
  assign _2Q = and_1_out ? s_r_ff_2_q : 1'bz;  // Controlled_Buffer controlled_buffer_2
  assign _3Q = and_1_out ? s_r_ff_3_q : 1'bz;  // Controlled_Buffer controlled_buffer_3
  assign _4Q = and_1_out ? s_r_ff_4_q : 1'bz;  // Controlled_Buffer controlled_buffer_4
  not not_4 (not_4_out, nG1);
  and and_10 (and_10_out, not_4_out, not_5_out);
  not not_5 (not_5_out, nG2);
endmodule

// SN7408
module _7408 (
  input  _1__1A,
  input  _14__Vcc,
  input  _2__1B,
  input  _13__4B,
  input  _12__4A,
  input  _4__2A,
  input  _5__2B,
  input  _10__3B,
  input  _9__3A,
  input  _7__GND,
  output _3__1Y,
  output _11__4Y,
  output _6__2Y,
  output _8__3Y
);

  and and_1 (_3__1Y, _2__1B, _1__1A);
  and and_2 (_6__2Y, _5__2B, _4__2A);
  and and_3 (_11__4Y, _13__4B, _12__4A);
  and and_4 (_8__3Y, _10__3B, _9__3A);

  // Notes on the sheet:
  //   7408: quad AND
endmodule

// SN7404
module _7404 (
  input  _1__1A,
  input  _14__Vcc,
  input  _13__6A,
  input  _3__2A,
  input  _11__5A,
  input  _5__3A,
  input  _9__4A,
  input  _7__GND,
  output _2__1Y,
  output _12__6Y,
  output _4__2Y,
  output _10__5Y,
  output _6__3Y,
  output _8__4Y
);

  not not_1 (_2__1Y, _1__1A);
  not not_2 (_4__2Y, _3__2A);
  not not_3 (_6__3Y, _5__3A);
  not not_4 (_12__6Y, _13__6A);
  not not_5 (_10__5Y, _11__5A);
  not not_6 (_8__4Y, _9__4A);

  // Notes on the sheet:
  //   7407: hex inverter
endmodule

// SN74151A
module _74151 (
  input  _1__D3,
  input  _16__Vcc,
  input  _2__D2,
  input  _15__D4,
  input  _3__D1,
  input  _14__D5,
  input  _4__D0,
  input  _13__D6,
  input  _12__D7,
  input  _11__A,
  input  _7__nG,
  input  _10__B,
  input  _8__GND,
  input  _9__C,
  output _5__Y,
  output _6__W
);

  wire multiplexer_1_out, not_2_out;

  not not_1 (_5__Y, _6__W);
  or or_1 (_6__W, not_2_out, _7__nG);
  not not_2 (not_2_out, multiplexer_1_out);
  Multiplexer #(.select(3), .enable("false")) multiplexer_1 (
    .in0(_4__D0), .in1(_3__D1), .in2(_2__D2), .in3(_1__D3), .in4(_15__D4), .in5(_14__D5), .in6(_13__D6),
    .in7(_12__D7), .out(multiplexer_1_out), .sel({_9__C, _10__B, _11__A}));

  // Notes on the sheet:
  //   74151: 8-Line to 1-Line Multiplexer
endmodule

// SN7474
module _7474 (
  input  _1__CLR1,
  input  _14__Vcc,
  input  _2__D1,
  input  _13__CLR2,
  input  _3__CLK1,
  input  _12__D2,
  input  _4__PR1,
  input  _11__CLK2,
  input  _10__PR2,
  input  _7__GND,
  output _5__Q1,
  output _6__nQ1,
  output _9__Q2,
  output _8__nQ2
);

  D_Flip_Flop d_ff_1 (
    .clk(_3__CLK1), .D(_2__D1), .Q(_5__Q1), .Qn(_6__nQ1), .preset(_4__PR1), .reset(_1__CLR1));  // open: en
  D_Flip_Flop d_ff_2 (
    .clk(_11__CLK2), .D(_12__D2), .Q(_9__Q2), .Qn(_8__nQ2), .preset(_10__PR2), .reset(_13__CLR2));  // open: en

  // Notes on the sheet:
  //   7474: dual D-type flip flop
endmodule

// SN74161
module _74161 (
  input  _1__nMR,
  input  _16__Vcc,
  input  _2__CP,
  input  _3__D0,
  input  _4__D1,
  input  _5__D2,
  input  _6__D3,
  input  _7__CEP,
  input  _10__CET,
  input  _8__GND,
  input  _9__nPE,
  output _15__TC,
  output _14__Q0,
  output _13__Q1,
  output _12__Q2,
  output _11__O3
);

  wire and_1_out, counter_1_carry, not_1_out, not_2_out;

  not not_1 (not_1_out, _1__nMR);
  and and_1 (and_1_out, _7__CEP, _9__nPE, _10__CET);
  Counter #(.width(4), .max('hf)) counter_1 (
    .load(not_2_out), .D({_6__D3, _5__D2, _4__D1, _3__D0}), .count(and_1_out),
    .Q({_11__O3, _12__Q2, _13__Q1, _14__Q0}), .carry(counter_1_carry), .clk(_2__CP), .clr(not_1_out));
  and and_2 (_15__TC, counter_1_carry, _10__CET);
  not not_2 (not_2_out, _9__nPE);

  // Notes on the sheet:
  //   74161: Synchronous 4-bit Binary Counter with Asynchronous Clear 
endmodule

// SN7432
module _7432 (
  input  _1__1A,
  input  _14__Vcc,
  input  _2__1B,
  input  _13__4B,
  input  _12__4A,
  input  _4__2A,
  input  _5__2B,
  input  _10__3B,
  input  _9__3A,
  input  _7__GND,
  output _3__1Y,
  output _11__4Y,
  output _6__2Y,
  output _8__3Y
);

  or or_1 (_3__1Y, _2__1B, _1__1A);
  or or_2 (_6__2Y, _5__2B, _4__2A);
  or or_3 (_11__4Y, _13__4B, _12__4A);
  or or_4 (_8__3Y, _10__3B, _9__3A);

  // Notes on the sheet:
  //   7432: quad OR
endmodule

// SN74153
module _74153 (
  input  _1__nG1,
  input  _16__Vcc,
  input  _2__B,
  input  _15__nG2,
  input  _3__1C3,
  input  _14__A,
  input  _4__1C2,
  input  _13__2C3,
  input  _5__1C1,
  input  _12__2C2,
  input  _6__1C0,
  input  _11__2C1,
  input  _10__2C0,
  input  _8__GND,
  output _7__Y1,
  output _9__Y2
);

  wire multiplexer_1_out, multiplexer_2_out, not_1_out, not_2_out;

  not not_1 (not_1_out, _1__nG1);
  Multiplexer #(.select(2), .enable("false")) multiplexer_1 (
    .in0(_6__1C0), .in1(_5__1C1), .in2(_4__1C2), .in3(_3__1C3), .out(multiplexer_1_out), .sel({_2__B, _14__A}));
  and and_1 (_7__Y1, multiplexer_1_out, not_1_out);
  not not_2 (not_2_out, _15__nG2);
  Multiplexer #(.select(2), .enable("false")) multiplexer_2 (
    .in0(_10__2C0), .in1(_11__2C1), .in2(_12__2C2), .in3(_13__2C3), .out(multiplexer_2_out),
    .sel({_2__B, _14__A}));
  and and_2 (_9__Y2, multiplexer_2_out, not_2_out);

  // Notes on the sheet:
  //   74153: Dual 4-Line to 1-Line Multiplexer
endmodule

// SN74LS139A
module _74139 (
  input  _1__1G,
  input  _16__Vcc,
  input  _2__1A,
  input  _15__2G,
  input  _3__1B,
  input  _14__2A,
  input  _13__2B,
  input  _8__GND,
  output _4__1Y0,
  output _5__1Y1,
  output _12__2Y0,
  output _6__1Y2,
  output _11__2Y1,
  output _7__1Y3,
  output _10__2Y2,
  output _9__2Y3
);

  wire decoder_1_out0, decoder_1_out1, decoder_1_out2, decoder_1_out3, decoder_2_out0, decoder_2_out1,
       decoder_2_out2, decoder_2_out3, not_1_out, not_2_out, not_3_out, not_4_out, not_5_out, not_6_out,
       not_7_out, not_8_out, not_9_out, not_10_out;

  not not_1 (not_1_out, _1__1G);
  and and_1 (_4__1Y0, not_1_out, not_2_out);
  not not_2 (not_2_out, decoder_1_out0);
  and and_2 (_5__1Y1, not_1_out, not_3_out);
  not not_3 (not_3_out, decoder_1_out1);
  and and_3 (_6__1Y2, not_1_out, not_4_out);
  not not_4 (not_4_out, decoder_1_out2);
  and and_4 (_7__1Y3, not_1_out, not_5_out);
  not not_5 (not_5_out, decoder_1_out3);
  Decoder #(.select(2), .enable("false")) decoder_1 (
    .out0(decoder_1_out0), .out1(decoder_1_out1), .out2(decoder_1_out2), .out3(decoder_1_out3),
    .sel({_3__1B, _2__1A}));
  Decoder #(.select(2), .enable("false")) decoder_2 (
    .out0(decoder_2_out0), .out1(decoder_2_out1), .out2(decoder_2_out2), .out3(decoder_2_out3),
    .sel({_13__2B, _14__2A}));
  not not_6 (not_6_out, _15__2G);
  not not_7 (not_7_out, decoder_2_out0);
  not not_8 (not_8_out, decoder_2_out1);
  not not_9 (not_9_out, decoder_2_out2);
  not not_10 (not_10_out, decoder_2_out3);
  and and_5 (_12__2Y0, not_6_out, not_7_out);
  and and_6 (_11__2Y1, not_6_out, not_8_out);
  and and_7 (_10__2Y2, not_6_out, not_9_out);
  and and_8 (_9__2Y3, not_6_out, not_10_out);

  // Notes on the sheet:
  //   74139: Dual 2-Line to 4-Line Decoder
endmodule

// SN74157
module _74157 (
  input  _1__S,
  input  _16__Vcc,
  input  _2__A1,
  input  _15__G,
  input  _3__B1,
  input  _14__A4,
  input  _13__B4,
  input  _5__A2,
  input  _6__B2,
  input  _11__A3,
  input  _10__B3,
  input  _8__GND,
  output _4__Y1,
  output _12__Y4,
  output _7__Y2,
  output _9__Y3
);

  wire multiplexer_1_out, multiplexer_2_out, multiplexer_3_out, multiplexer_4_out, not_1_out;

  Multiplexer #(.enable("false")) multiplexer_1 (.in0(_2__A1), .in1(_3__B1), .out(multiplexer_1_out), .sel(_1__S));
  and and_1 (_4__Y1, multiplexer_1_out, not_1_out);
  Multiplexer #(.enable("false")) multiplexer_2 (.in0(_5__A2), .in1(_6__B2), .out(multiplexer_2_out), .sel(_1__S));
  and and_2 (_7__Y2, multiplexer_2_out, not_1_out);
  not not_1 (not_1_out, _15__G);
  Multiplexer #(.enable("false")) multiplexer_3 (.in0(_14__A4), .in1(_13__B4), .out(multiplexer_3_out), .sel(_1__S));
  and and_3 (_12__Y4, multiplexer_3_out, not_1_out);
  Multiplexer #(.enable("false")) multiplexer_4 (.in0(_11__A3), .in1(_10__B3), .out(multiplexer_4_out), .sel(_1__S));
  and and_4 (_9__Y3, multiplexer_4_out, not_1_out);

  // Notes on the sheet:
  //   74157: Quad 2-Line to 1-Line Multiplexer
endmodule
