// Logisim project DD_DESIGN_ASSIGNMENT (1).circ as structural Verilog: 1 circuit, main circuit main
module main (
  input  in_1,
  input  in_2,
  input  in_3,
  input  in_4,
  input  in_5,
  input  in_6,
  input  in_7,
  input  in_8,
  input  in_9,
  input  in_10,
  input  in_11,
  input  in_12,
  input  in_13,
  input  in_14,
  input  in_15,
  input  in_16,
  input  in_17,
  input  in_18,
  input  in_19,
  input  in_20,
  input  in_21,
  input  in_22,
  input  in_23,
  input  in_24,
  input  in_25,
  input  in_26,
  input  in_27,
  input  in_28,
  input  in_29,
  input  in_30,
  input  in_31,
  input  in_32,
  input  in_33,
  input  in_34,
  input  in_35,
  input  in_36,
  output out_37,
  output out_38,
  output out_39,
  output out_40,
  output out_41,
  output out_42,
  output out_43,
  output out_44
);

  wire and_1_out, and_2_out, and_4_out, and_5_out, and_6_out, and_7_out, comparator_1_eq, comparator_2_eq,
       controlled_buffer_1_out, controlled_buffer_2_out, controlled_buffer_13_out, controlled_buffer_14_out,
       controlled_buffer_15_out, controlled_buffer_16_out, nand_1_out, not_1_out, not_2_out, not_3_out,
       not_4_out, not_5_out, not_6_out, not_7_out, not_8_out, not_9_out, not_10_out, not_11_out, or_1_out,
       or_2_out, or_3_out, or_4_out, shift_register_2_q0, shift_register_2_q1, shift_register_2_q2,
       shift_register_2_q3;
  wire [3:0] controlled_buffer_6_out, controlled_buffer_10_out, shift_register_1_q3;

  assign controlled_buffer_1_out = in_33 ? in_33 : 1'bz;  // Controlled_Buffer controlled_buffer_1
  assign controlled_buffer_2_out = in_21 ? in_21 : 1'bz;  // Controlled_Buffer controlled_buffer_2
  not not_1 (not_1_out, in_33);
  assign controlled_buffer_6_out[3] = controlled_buffer_1_out ? in_24 : 1'bz;  // Controlled_Buffer controlled_buffer_3
  assign controlled_buffer_6_out[2] = controlled_buffer_1_out ? in_25 : 1'bz;  // Controlled_Buffer controlled_buffer_4
  assign controlled_buffer_6_out[1] = controlled_buffer_1_out ? in_26 : 1'bz;  // Controlled_Buffer controlled_buffer_5
  assign controlled_buffer_6_out[0] = controlled_buffer_1_out ? in_27 : 1'bz;  // Controlled_Buffer controlled_buffer_6
  not not_2 (not_2_out, in_21);
  assign controlled_buffer_10_out[3] = controlled_buffer_2_out ? in_3 : 1'bz;  // Controlled_Buffer controlled_buffer_7
  assign controlled_buffer_10_out[2] = controlled_buffer_2_out ? in_6 : 1'bz;  // Controlled_Buffer controlled_buffer_8
  assign controlled_buffer_10_out[1] = controlled_buffer_2_out ? in_9 : 1'bz;  // Controlled_Buffer controlled_buffer_9
  assign controlled_buffer_10_out[0] = controlled_buffer_2_out ? in_12 : 1'bz;  // Controlled_Buffer controlled_buffer_10
  not not_3 (not_3_out, comparator_1_eq);
  Comparator #(.width(4)) comparator_1 (
    .a(controlled_buffer_6_out), .b({in_28, in_30, in_32, in_35}), .eq(comparator_1_eq));  // open: gt, lt
  assign out_43 = controlled_buffer_1_out ? not_3_out : 1'bz;  // Controlled_Buffer controlled_buffer_11
  not not_4 (not_4_out, comparator_2_eq);
  Comparator #(.width(4)) comparator_2 (
    .a(controlled_buffer_10_out), .b({in_15, in_17, in_19, in_22}), .eq(comparator_2_eq));  // open: gt, lt
  assign out_39 = controlled_buffer_2_out ? not_4_out : 1'bz;  // Controlled_Buffer controlled_buffer_12
  not not_5 (not_5_out, out_44);
  Shift_Register #(.length(4)) shift_register_1 (
    .shift(not_5_out), .in(out_43), .clk(not_1_out), .q0(shift_register_1_q3[3]),
    .q1(shift_register_1_q3[2]), .q2(shift_register_1_q3[1]), .q3(shift_register_1_q3[0]));  // open: out, load, clr, d0, d1, d2, d3
  not not_6 (not_6_out, out_42);
  Comparator #(.width(4)) comparator_3 (
    .a(shift_register_1_q3), .b({in_36, in_34, in_31, in_29}), .eq(out_44));  // open: gt, lt
  LED led_1 (.in(out_44));
  Shift_Register #(.length(4)) shift_register_2 (
    .shift(not_6_out), .in(out_39), .clk(not_2_out), .clr(in_23), .q0(shift_register_2_q0),
    .q1(shift_register_2_q1), .q2(shift_register_2_q2), .q3(shift_register_2_q3));  // open: out, load, d0, d1, d2, d3
  and and_1 (and_1_out, shift_register_2_q0, shift_register_2_q1);
  and and_2 (and_2_out, shift_register_2_q2, shift_register_2_q3);
  and and_3 (out_42, and_1_out, and_2_out);
  LED led_2 (.in(out_42));
  not not_7 (not_7_out, shift_register_2_q0);
  not not_8 (not_8_out, shift_register_2_q1);
  not not_9 (not_9_out, shift_register_2_q2);
  not not_10 (not_10_out, shift_register_2_q1);
  not not_11 (not_11_out, shift_register_2_q2);
  nand nand_1 (nand_1_out, shift_register_2_q2, shift_register_2_q1, shift_register_2_q0);
  and and_4 (and_4_out, shift_register_2_q1, shift_register_2_q3, shift_register_2_q2);
  and and_5 (and_5_out, shift_register_2_q0, shift_register_2_q1, not_9_out);
  and and_6 (and_6_out, shift_register_2_q0, shift_register_2_q3, shift_register_2_q1);
  or or_1 (or_1_out, not_7_out, and_4_out);
  or or_2 (or_2_out, not_7_out, shift_register_2_q2, not_8_out);
  or or_3 (or_3_out, and_5_out, and_6_out);
  or or_4 (or_4_out, not_10_out, not_11_out, shift_register_2_q3);
  _7_Segment_Display u_7_segment_display_1 (
    .g(nand_1_out), .f(or_1_out), .a(and_7_out), .b(in_13), .e(or_3_out), .d(and_7_out), .c(or_2_out));  // open: dp
  and and_7 (and_7_out, shift_register_2_q0, or_4_out);
  assign controlled_buffer_13_out = in_2 ? in_1 : 1'bz;  // Controlled_Buffer controlled_buffer_13
  assign controlled_buffer_14_out = in_5 ? in_4 : 1'bz;  // Controlled_Buffer controlled_buffer_14
  assign controlled_buffer_15_out = in_8 ? in_7 : 1'bz;  // Controlled_Buffer controlled_buffer_15
  assign controlled_buffer_16_out = in_11 ? in_10 : 1'bz;  // Controlled_Buffer controlled_buffer_16
  xnor xnor_1 (out_37, controlled_buffer_13_out, in_14);
  xnor xnor_2 (out_38, controlled_buffer_14_out, in_16);
  xnor xnor_3 (out_40, controlled_buffer_15_out, in_18);
  xnor xnor_4 (out_41, controlled_buffer_16_out, in_20);

  // Notes on the sheet:
  //   in_9: pull=up
  //   in_26: pull=up
  //   ATTEMPT1
  //   i/p=1 for enable and =0 for reset
  //   i/p=1 for enable and =0 for reset
  //   ATTEMPT3
  //   In case the owner has by mistake entered 4 wrong passwords and wants to get the system reset froom the service centre 
  //   Correct i/p of the passwrod gives o/p=0 
  //   Correct i/p of the passwrod gives o/p=0 
  //   Reset the Shift Register
  //   To detect f there are 4 wrong inputs
  //   1)How to reset the i/p automatically
  //   To detect f there are 4 wrong inputs
  //   ALARM
  //   CONCERNS
  //   ALARM
  //   ATTEMPT 2
endmodule
