// Logisim project DD_DESIGN_ASSIGNMENT.circ as structural Verilog: 1 circuit, main circuit main
module main (
  input  in_1,
  input  in_2,
  input  in_3,
  input  in_4,
  input  in_5,
  input  in_6,
  input  in_7,
  input  in_8,
  input  in_9,
  input  in_10,
  input  in_11,
  input  in_12,
  input  in_13,
  input  in_14,
  input  in_15,
  input  in_16,
  input  in_17,
  input  in_18,
  input  in_19,
  input  in_20,
  input  in_21,
  output out_22,
  output out_23,
  output out_24,
  output out_25,
  output out_26,
  output out_27
);

  wire and_1_out, and_3_out, comparator_1_eq, controlled_buffer_1_out, controlled_buffer_7_out,
       controlled_buffer_8_out, controlled_buffer_9_out, controlled_buffer_10_out, not_1_out, not_2_out,
       not_3_out, shift_register_1_q0, shift_register_1_q1, shift_register_1_q2, shift_register_1_q3;
  wire [3:0] controlled_buffer_5_out;

  assign controlled_buffer_1_out = in_17 ? in_17 : 1'bz;  // Controlled_Buffer controlled_buffer_1
  Counter counter_1 ();  // open: load, D, count, Q, carry, clk, clr
  not not_1 (not_1_out, in_17);
  assign controlled_buffer_5_out[3] = controlled_buffer_1_out ? in_2 : 1'bz;  // Controlled_Buffer controlled_buffer_2
  assign controlled_buffer_5_out[2] = controlled_buffer_1_out ? in_4 : 1'bz;  // Controlled_Buffer controlled_buffer_3
  assign controlled_buffer_5_out[1] = controlled_buffer_1_out ? in_7 : 1'bz;  // Controlled_Buffer controlled_buffer_4
  assign controlled_buffer_5_out[0] = controlled_buffer_1_out ? in_9 : 1'bz;  // Controlled_Buffer controlled_buffer_5
  not not_2 (not_2_out, comparator_1_eq);
  Comparator #(.width(4)) comparator_1 (
    .a(controlled_buffer_5_out), .b({in_11, in_13, in_15, in_16}), .eq(comparator_1_eq));  // open: gt, lt
  assign out_23 = controlled_buffer_1_out ? not_2_out : 1'bz;  // Controlled_Buffer controlled_buffer_6
  not not_3 (not_3_out, out_27);
  Shift_Register #(.length(4)) shift_register_1 (
    .shift(not_3_out), .in(out_23), .clk(not_1_out), .q0(shift_register_1_q0), .q1(shift_register_1_q1),
    .q2(shift_register_1_q2), .q3(shift_register_1_q3));  // open: out, load, clr, d0, d1, d2, d3
  and and_1 (and_1_out, shift_register_1_q0, shift_register_1_q1);
  and and_2 (out_27, and_1_out, and_3_out);
  and and_3 (and_3_out, shift_register_1_q2, shift_register_1_q3);
  LED led_1 (.in(out_27));
  assign controlled_buffer_7_out = in_3 ? in_1 : 1'bz;  // Controlled_Buffer controlled_buffer_7
  assign controlled_buffer_8_out = in_6 ? in_5 : 1'bz;  // Controlled_Buffer controlled_buffer_8
  assign controlled_buffer_9_out = in_10 ? in_8 : 1'bz;  // Controlled_Buffer controlled_buffer_9
  assign controlled_buffer_10_out = in_14 ? in_12 : 1'bz;  // Controlled_Buffer controlled_buffer_10
  xnor xnor_1 (out_22, controlled_buffer_7_out, in_18);
  xnor xnor_2 (out_24, controlled_buffer_8_out, in_19);
  xnor xnor_3 (out_25, controlled_buffer_9_out, in_20);
  xnor xnor_4 (out_26, controlled_buffer_10_out, in_21);

  // Notes on the sheet:
  //   in_7: pull=up
  //   i/p=1 for enable and =0 for reset
  //   Correct i/p of the passwrod gives o/p=0 
  //   1)How to reset the i/p automatically
  //   2)Can we use a shift register 
  //   3)How to lock the car forever
  //   ALARM
  //   To detect f there are 4 wrong inputs
  //   CONCERNS
endmodule
