// Logisim project Design.circ as structural Verilog: 3 circuits, main circuit main
module main (
  input  X3,
  input  X2,
  input  X3_2,
  input  X1,
  input  X2_2,
  input  X0,
  input  X1_2,
  input  in_8,
  input  X0_2,
  input  Reset,
  input  A3,
  input  A2,
  input  A1,
  input  A0,
  input  A3_2,
  input  A2_2,
  input  A1_2,
  input  A0_2,
  input  X3_3,
  input  X3_4,
  input  X2_3,
  input  X2_4,
  input  X1_3,
  input  X1_4,
  input  X0_3,
  input  X0_4,
  input  in_27,
  input  A3_3,
  input  A2_3,
  input  A1_3,
  input  A0_3,
  input  A3_4,
  input  A2_4,
  input  A1_4,
  input  A0_4,
  output Locked,
  output Unlocked,
  output Lock
);

  wire and_1_out, and_2_out, and_3_out, and_4_out, and_5_out, and_6_out, and_7_out, and_8_out, and_9_out,
       and_10_out, and_11_out, and_12_out, and_13_out, and_15_out, and_16_out, button_1_out, button_2_out,
       clock_1_out, comparator_1_eq, comparator_2_lt, comparator_3_eq, comparator_5_eq, comparator_6_eq,
       controlled_buffer_1_out, ENTER_2_out, ENTER_out, LED_Display_Ckt_a, LED_Display_Ckt_b,
       LED_Display_Ckt_d, LED_Display_Ckt_e, LED_Display_Ckt_f, LED_Display_Ckt_g, not_1_out, not_2_out,
       not_3_out, not_6_out, not_7_out, not_8_out, not_9_out, not_10_out, not_11_out, not_12_out, not_13_out,
       or_2_out, or_3_out, or_4_out, or_5_out, or_6_out, or_7_out, register_5_q, register_6_q,
       shift_register_2_q0, shift_register_2_q1, shift_register_2_q2, shift_register_2_q3, undriven,
       Unlock_Button__inside_the_car_out;
  wire [2:0] counter_2_q;
  wire [3:0] multiplexer_1_out, multiplexer_2_out, register_1_q, register_2_q, register_3_q, register_4_q;
  wire [4:0] counter_1_q;

  Button ENTER (.out(ENTER_out));
  not not_1 (not_1_out, ENTER_out);
  Comparator #(.width(4)) comparator_1 (
    .a({X3_2, X2_2, X1_2, X0_2}), .b(register_1_q), .eq(comparator_1_eq));  // open: gt, lt
  Register #(.width(4)) register_1 (.D({A3, A2, A1, A0}), .Q(register_1_q), .clk(ENTER_out));  // open: en, clr
  Clock clock_1 (.out(clock_1_out));
  and and_1 (and_1_out, clock_1_out, comparator_1_eq);
  not not_2 (not_2_out, comparator_1_eq);
  assign controlled_buffer_1_out = and_2_out ? not_2_out : 1'bz;  // Controlled_Buffer controlled_buffer_1
  and and_2 (and_2_out, ENTER_out, not_3_out);
  and and_3 (and_3_out, not_1_out, not_3_out);
  Counter #(.width(5), .max('h1f), .ongoal("stay")) counter_1 (
    .Q(counter_1_q), .clk(and_1_out), .clr(Unlock_Button__inside_the_car_out));  // open: load, D, count, carry
  Counter #(.width(3), .max('h7)) counter_2 (
    .load(comparator_1_eq), .D(3'b000), .count(controlled_buffer_1_out), .Q(counter_2_q), .clk(and_3_out),
    .clr(Reset));  // open: carry
  Comparator #(.width(5), .mode("unsigned")) comparator_2 (
    .a(5'b11100), .b(counter_1_q), .lt(comparator_2_lt));  // open: gt, eq
  Comparator #(.width(3)) comparator_3 (.a(counter_2_q), .b(3'b100), .eq(comparator_3_eq));  // open: gt, lt
  Button ENTER_2 (.out(ENTER_2_out));
  not not_3 (not_3_out, comparator_3_eq);
  // NOT_Gate not_4 has open pins: in=ENTER_2_out, out=open
  or or_1 (Locked, comparator_2_lt, comparator_3_eq);
  Button Unlock_Button__inside_the_car (.out(Unlock_Button__inside_the_car_out));
  Comparator #(.width(4)) comparator_4 (.a({X3_4, X2_4, X1_4, X0_4}), .b(register_2_q));  // open: gt, eq, lt
  Register #(.width(4)) register_2 (
    .D({A3_3, A2_3, A1_3, A0_3}), .Q(register_2_q), .clk(ENTER_2_out), .clr(undriven));  // open: en
  LED Alarm (.in(comparator_3_eq));
  not not_5 (Unlocked, Locked);
  LED_Display LED_Display_Ckt (
    .Input(counter_2_q), .a(LED_Display_Ckt_a), .b(LED_Display_Ckt_b), .d(LED_Display_Ckt_d),
    .e(LED_Display_Ckt_e), .f(LED_Display_Ckt_f), .g(LED_Display_Ckt_g));
  _7_Segment_Display u_7_segment_display_1 (
    .g(LED_Display_Ckt_g), .f(LED_Display_Ckt_a), .a(LED_Display_Ckt_b), .b(1'b1), .e(LED_Display_Ckt_f),
    .d(LED_Display_Ckt_e), .c(LED_Display_Ckt_d));  // open: dp
  Shift_Register #(.length(1)) shift_register_1 ();  // open: shift, in, clk, out, load, clr, d0, q0
  Button button_1 (.out(button_1_out));
  Button button_2 (.out(button_2_out));
  Multiplexer #(.width(4)) multiplexer_1 (
    .in0({A3_2, A2_2, A1_2, A0_2}), .in1({X3, X2, X1, X0}), .out(multiplexer_1_out), .sel(and_4_out),
    .en(in_8));
  and and_4 (and_4_out, in_8, register_5_q);
  Multiplexer #(.width(4)) multiplexer_2 (
    .in0({A3_4, A2_4, A1_4, A0_4}), .in1({X3_3, X2_3, X1_3, X0_3}), .out(multiplexer_2_out),
    .sel(register_6_q));  // open: en
  Comparator #(.width(4)) comparator_5 (.a({X3, X2, X1, X0}), .b(register_3_q), .eq(comparator_5_eq));  // open: gt, lt
  Register #(.width(4)) register_3 (.D(multiplexer_1_out), .Q(register_3_q), .clk(button_1_out));  // open: en, clr
  Comparator #(.width(4)) comparator_6 (
    .a({X3_3, X2_3, X1_3, X0_3}), .b(register_4_q), .eq(comparator_6_eq));  // open: gt, lt
  Register #(.width(4)) register_4 (.D(multiplexer_2_out), .Q(register_4_q), .clk(button_2_out));  // open: en, clr
  Register #(.width(1)) register_5 (.D(comparator_5_eq), .en(in_8), .Q(register_5_q), .clk(button_1_out));  // open: clr
  Register #(.width(1)) register_6 (
    .D(comparator_6_eq), .en(in_27), .Q(register_6_q), .clk(button_2_out));  // open: clr
  not not_6 (not_6_out, Lock);
  Shift_Register #(.length(4)) shift_register_2 (
    .shift(not_6_out), .q0(shift_register_2_q0), .q1(shift_register_2_q1), .q2(shift_register_2_q2),
    .q3(shift_register_2_q3));  // open: in, clk, out, load, clr, d0, d1, d2, d3
  not not_7 (not_7_out, shift_register_2_q0);
  not not_8 (not_8_out, shift_register_2_q0);
  not not_9 (not_9_out, shift_register_2_q1);
  not not_10 (not_10_out, shift_register_2_q2);
  not not_11 (not_11_out, shift_register_2_q1);
  not not_12 (not_12_out, shift_register_2_q2);
  and and_5 (and_5_out, shift_register_2_q0, shift_register_2_q1);
  and and_6 (and_6_out, and_5_out, shift_register_2_q2);
  not not_13 (not_13_out, and_6_out);
  and and_7 (and_7_out, shift_register_2_q1, shift_register_2_q2);
  and and_8 (and_8_out, and_7_out, shift_register_2_q3);
  or or_2 (or_2_out, not_8_out, not_9_out);
  or or_3 (or_3_out, or_2_out, shift_register_2_q2);
  and and_9 (and_9_out, shift_register_2_q0, shift_register_2_q1);
  and and_10 (and_10_out, and_9_out, not_10_out);
  and and_11 (and_11_out, shift_register_2_q0, shift_register_2_q1);
  and and_12 (and_12_out, and_11_out, shift_register_2_q3);
  or or_4 (or_4_out, not_11_out, not_12_out);
  or or_5 (or_5_out, or_4_out, shift_register_2_q3);
  and and_13 (and_13_out, shift_register_2_q3, shift_register_2_q2);
  and and_14 (Lock, and_13_out, and_15_out);
  and and_15 (and_15_out, shift_register_2_q1, shift_register_2_q0);
  or or_6 (or_6_out, not_7_out, and_8_out);
  or or_7 (or_7_out, and_10_out, and_12_out);
  and and_16 (and_16_out, or_5_out, shift_register_2_q0);
  _7_Segment_Display u_7_segment_display_2 (
    .g(not_13_out), .f(or_6_out), .a(and_16_out), .b(1'b1), .e(or_7_out), .d(and_16_out), .c(or_3_out));  // open: dp
  LED Alarm_2 (.in(Lock));

  // Notes on the sheet:
  //   This reset can be used internally to reset if user takes it to repair center
endmodule

// LED CKT
module LED_Display (
  input  [2:0] Input,
  output a,
  output b,
  output d,
  output e,
  output f,
  output g
);

  wire not_1_out;

  not not_1 (not_1_out, Input[0]);
  Multiplexer #(.select(2)) multiplexer_1 (
    .in0(not_1_out), .in1(1'b0), .in2(1'b1), .in3(1'b1), .out(a), .sel(Input[2:1]));  // open: en
  Multiplexer #(.select(2)) multiplexer_2 (
    .in0(Input[0]), .in1(not_1_out), .in2(not_1_out), .in3(1'b0), .out(b), .sel(Input[2:1]));  // open: en
  Multiplexer #(.select(2)) multiplexer_3 (
    .in0(1'b1), .in1(Input[0]), .in2(1'b1), .in3(1'b1), .out(d), .sel(Input[2:1]));  // open: en
  Multiplexer #(.select(2)) multiplexer_4 (
    .in0(Input[0]), .in1(not_1_out), .in2(not_1_out), .in3(1'b0), .out(e), .sel(Input[2:1]));  // open: en
  Multiplexer #(.select(2)) multiplexer_5 (
    .in0(1'b0), .in1(not_1_out), .in2(not_1_out), .in3(1'b0), .out(f), .sel(Input[2:1]));  // open: en
  Multiplexer #(.select(2)) multiplexer_6 (
    .in0(1'b1), .in1(not_1_out), .in2(Input[0]), .in3(1'b1), .out(g), .sel(Input[2:1]));  // open: en
endmodule

module random (
);

  // AND_Gate and_1 is placed but not wired
endmodule
