// Logisim project Design_updated.circ as structural Verilog: 3 circuits, main circuit main
module main (
  input  [3:0] in_1,
  input  [3:0] in_2,
  input  Door_Closed,
  input  [2:0] in_4,
  input  [2:0] in_5,
  input  X3,
  input  X2,
  input  X1,
  input  [2:0] in_9,
  input  X3_2,
  input  X0,
  input  X2_2,
  input  Factory_Reset,
  input  Change_Password,
  input  X1_2,
  input  X0_2,
  input  [3:0] Original_Password,
  input  A3,
  input  A2,
  input  A1,
  input  A0,
  input  X3_3,
  input  X2_3,
  input  X1_3,
  input  X0_3,
  input  in_26,
  input  A3_2,
  input  A2_2,
  input  A1_2,
  input  A0_2,
  input  X3_4,
  input  X2_4,
  input  X1_4,
  input  X0_4,
  input  [3:0] Original_Password_2,
  output Locked,
  output Unlocked,
  output Lock
);

  wire and_1_out, and_2_out, and_3_out, and_4_out, and_5_out, and_6_out, and_7_out, and_8_out, and_9_out,
       and_10_out, and_11_out, and_12_out, and_13_out, and_14_out, and_16_out, and_17_out, button_1_out,
       clock_1_out, comparator_2_eq, comparator_3_eq, comparator_4_eq, comparator_4_lt, comparator_5_eq,
       comparator_6_eq, comparator_8_eq, controlled_buffer_1_out, decoder_1_out1, decoder_1_out3,
       ENTER_2_out, ENTER_3_out, LED_Display_Ckt_a, LED_Display_Ckt_b, LED_Display_Ckt_d, LED_Display_Ckt_e,
       LED_Display_Ckt_f, LED_Display_Ckt_g, not_1_out, not_2_out, not_3_out, not_6_out, not_7_out,
       not_9_out, not_10_out, not_11_out, not_12_out, not_13_out, not_14_out, not_15_out, not_16_out,
       or_1_out, or_2_out, or_4_out, or_5_out, or_6_out, or_7_out, or_8_out, or_9_out, or_10_out,
       register_1_q, register_2_q, register_5_q, shift_register_1_q0, shift_register_1_q1,
       shift_register_1_q2, shift_register_1_q3, undriven_2, undriven_3, undriven_4,
       Unlock_Button__inside_the_car_out;
  wire [1:0] not_4_out;
  wire [2:0] counter_2_q;
  wire [3:0] counter_1_q, multiplexer_1_out, multiplexer_2_out, multiplexer_3_out, Password_2_q, Password_q,
       register_3_q, register_4_q, undriven;

  Button ENTER (.out(not_4_out[1]));
  Comparator #(.width(4), .mode("unsigned")) comparator_1 (.a(in_1), .b(undriven));  // open: gt, eq, lt
  Multiplexer #(.width(4)) multiplexer_1 (
    .in0(Original_Password), .in1({X3, X2, X1, X0}), .out(multiplexer_1_out), .sel(and_1_out),
    .en(Change_Password));
  and and_1 (and_1_out, Change_Password, not_1_out, register_1_q);
  Comparator #(.width(4)) comparator_2 (.a({X3, X2, X1, X0}), .b(Password_q), .eq(comparator_2_eq));  // open: gt, lt
  Register #(.width(4)) Password (.D(multiplexer_1_out), .Q(Password_q), .clk(not_4_out[1]));  // open: en, clr
  not not_1 (not_1_out, Factory_Reset);
  Clock clock_1 (.out(clock_1_out));
  not not_2 (not_2_out, comparator_2_eq);
  Register #(.width(1)) register_1 (
    .D(comparator_2_eq), .en(Change_Password), .Q(register_1_q), .clk(and_2_out), .clr(Factory_Reset));
  and and_2 (and_2_out, not_4_out[1], not_3_out);
  not not_3 (not_3_out, register_1_q);
  and and_3 (and_3_out, clock_1_out, Door_Closed, comparator_2_eq);
  assign controlled_buffer_1_out = decoder_1_out3 ? not_2_out : 1'bz;  // Controlled_Buffer controlled_buffer_1
  or or_1 (or_1_out, comparator_2_eq, Factory_Reset);
  Decoder #(.select(2)) decoder_1 (
    .out1(decoder_1_out1), .out3(decoder_1_out3), .sel(not_4_out));  // open: out0, out2, en
  Counter #(.width(4), .max('hf), .ongoal("stay")) counter_1 (
    .Q(counter_1_q), .clk(and_3_out), .clr(or_2_out));  // open: load, D, count, carry
  or or_2 (or_2_out, Factory_Reset, Unlock_Button__inside_the_car_out);
  Counter #(.width(3), .max('h7)) counter_2 (
    .D(in_5), .count(controlled_buffer_1_out), .Q(counter_2_q), .clk(decoder_1_out1), .clr(or_1_out));  // open: load, carry
  Comparator #(.width(4), .mode("unsigned")) comparator_3 (
    .a(in_2), .b(counter_1_q), .eq(comparator_3_eq));  // open: gt, lt
  Comparator #(.width(3), .mode("unsigned")) comparator_4 (
    .a(in_4), .b(counter_2_q), .eq(comparator_4_eq), .lt(comparator_4_lt));  // open: gt
  Comparator #(.width(3)) comparator_5 (.a(counter_2_q), .b(in_9), .eq(comparator_5_eq));  // open: gt, lt
  not not_4 (not_4_out[0], comparator_5_eq);
  or or_3 (Locked, comparator_3_eq, or_4_out);
  or or_4 (or_4_out, comparator_4_eq, comparator_4_lt);
  Button Unlock_Button__inside_the_car (.out(Unlock_Button__inside_the_car_out));
  not not_5 (Unlocked, Locked);
  LED_Display LED_Display_Ckt (
    .Input(counter_2_q), .a(LED_Display_Ckt_a), .b(LED_Display_Ckt_b), .d(LED_Display_Ckt_d),
    .e(LED_Display_Ckt_e), .f(LED_Display_Ckt_f), .g(LED_Display_Ckt_g));
  LED Alarm (.in(comparator_5_eq));
  _7_Segment_Display u_7_segment_display_1 (
    .g(LED_Display_Ckt_g), .f(LED_Display_Ckt_a), .a(LED_Display_Ckt_b), .b(1'b1), .e(LED_Display_Ckt_f),
    .d(LED_Display_Ckt_e), .c(LED_Display_Ckt_d));  // open: dp
  Button ENTER_2 (.out(ENTER_2_out));
  Multiplexer #(.width(4)) multiplexer_2 (
    .in0(Original_Password_2), .in1({X3_4, X2_4, X1_4, X0_4}), .out(multiplexer_2_out), .sel(and_4_out));  // open: en
  and and_4 (and_4_out, undriven_2, not_6_out, register_2_q);
  Button button_1 (.out(button_1_out));
  Comparator #(.width(4)) comparator_6 (
    .a({X3_4, X2_4, X1_4, X0_4}), .b(Password_2_q), .eq(comparator_6_eq));  // open: gt, lt
  Register #(.width(4)) Password_2 (.D(multiplexer_2_out), .Q(Password_2_q), .clk(ENTER_2_out));  // open: en, clr
  not not_6 (not_6_out, undriven_3);
  Button ENTER_3 (.out(ENTER_3_out));
  Register #(.width(1)) register_2 (
    .D(comparator_6_eq), .en(undriven_2), .Q(register_2_q), .clk(and_5_out), .clr(undriven_3));
  and and_5 (and_5_out, ENTER_2_out, not_7_out);
  not not_7 (not_7_out, register_2_q);
  // NOT_Gate not_8 has open pins: in=ENTER_3_out, out=open
  Multiplexer #(.width(4)) multiplexer_3 (
    .in0({A3_2, A2_2, A1_2, A0_2}), .in1({X3_3, X2_3, X1_3, X0_3}), .out(multiplexer_3_out),
    .sel(register_5_q));  // open: en
  Comparator #(.width(4)) comparator_7 (.a({X3_2, X2_2, X1_2, X0_2}), .b(register_3_q));  // open: gt, eq, lt
  Register #(.width(4)) register_3 (
    .D({A3, A2, A1, A0}), .Q(register_3_q), .clk(ENTER_3_out), .clr(undriven_4));  // open: en
  Comparator #(.width(4)) comparator_8 (
    .a({X3_3, X2_3, X1_3, X0_3}), .b(register_4_q), .eq(comparator_8_eq));  // open: gt, lt
  Register #(.width(4)) register_4 (.D(multiplexer_3_out), .Q(register_4_q), .clk(button_1_out));  // open: en, clr
  Register #(.width(1)) register_5 (
    .D(comparator_8_eq), .en(in_26), .Q(register_5_q), .clk(button_1_out));  // open: clr
  not not_9 (not_9_out, Lock);
  Shift_Register #(.length(4)) shift_register_1 (
    .shift(not_9_out), .q0(shift_register_1_q0), .q1(shift_register_1_q1), .q2(shift_register_1_q2),
    .q3(shift_register_1_q3));  // open: in, clk, out, load, clr, d0, d1, d2, d3
  not not_10 (not_10_out, shift_register_1_q0);
  not not_11 (not_11_out, shift_register_1_q0);
  not not_12 (not_12_out, shift_register_1_q1);
  not not_13 (not_13_out, shift_register_1_q2);
  not not_14 (not_14_out, shift_register_1_q1);
  not not_15 (not_15_out, shift_register_1_q2);
  and and_6 (and_6_out, shift_register_1_q0, shift_register_1_q1);
  not not_16 (not_16_out, and_7_out);
  and and_7 (and_7_out, and_6_out, shift_register_1_q2);
  and and_8 (and_8_out, shift_register_1_q1, shift_register_1_q2);
  and and_9 (and_9_out, and_8_out, shift_register_1_q3);
  or or_5 (or_5_out, not_11_out, not_12_out);
  or or_6 (or_6_out, or_5_out, shift_register_1_q2);
  and and_10 (and_10_out, shift_register_1_q0, shift_register_1_q1);
  and and_11 (and_11_out, and_10_out, not_13_out);
  and and_12 (and_12_out, shift_register_1_q0, shift_register_1_q1);
  and and_13 (and_13_out, and_12_out, shift_register_1_q3);
  or or_7 (or_7_out, not_14_out, not_15_out);
  or or_8 (or_8_out, or_7_out, shift_register_1_q3);
  and and_14 (and_14_out, shift_register_1_q3, shift_register_1_q2);
  and and_15 (Lock, and_14_out, and_16_out);
  and and_16 (and_16_out, shift_register_1_q1, shift_register_1_q0);
  or or_9 (or_9_out, not_10_out, and_9_out);
  or or_10 (or_10_out, and_11_out, and_13_out);
  and and_17 (and_17_out, or_8_out, shift_register_1_q0);
  _7_Segment_Display u_7_segment_display_2 (
    .g(not_16_out), .f(or_9_out), .a(and_17_out), .b(1'b1), .e(or_10_out), .d(and_17_out), .c(or_6_out));  // open: dp
  LED Alarm_2 (.in(Lock));

  // Notes on the sheet:
  //   This will be 1 when user enters the car and closes the door
  //   This reset can be used internally to reset if user takes it to repair center
endmodule

// LED CKT
module LED_Display (
  input  [2:0] Input,
  output a,
  output b,
  output d,
  output e,
  output f,
  output g
);

  wire not_1_out;

  not not_1 (not_1_out, Input[0]);
  Multiplexer #(.select(2)) multiplexer_1 (
    .in0(not_1_out), .in1(1'b0), .in2(1'b1), .in3(1'b1), .out(a), .sel(Input[2:1]));  // open: en
  Multiplexer #(.select(2)) multiplexer_2 (
    .in0(Input[0]), .in1(not_1_out), .in2(not_1_out), .in3(1'b0), .out(b), .sel(Input[2:1]));  // open: en
  Multiplexer #(.select(2)) multiplexer_3 (
    .in0(1'b1), .in1(Input[0]), .in2(1'b1), .in3(1'b1), .out(d), .sel(Input[2:1]));  // open: en
  Multiplexer #(.select(2)) multiplexer_4 (
    .in0(Input[0]), .in1(not_1_out), .in2(not_1_out), .in3(1'b0), .out(e), .sel(Input[2:1]));  // open: en
  Multiplexer #(.select(2)) multiplexer_5 (
    .in0(1'b0), .in1(not_1_out), .in2(not_1_out), .in3(1'b0), .out(f), .sel(Input[2:1]));  // open: en
  Multiplexer #(.select(2)) multiplexer_6 (
    .in0(1'b1), .in1(not_1_out), .in2(Input[0]), .in3(1'b1), .out(g), .sel(Input[2:1]));  // open: en
endmodule

module random (
);

  // AND_Gate and_1 is placed but not wired
endmodule
