// Logisim project Design_updated_final.circ as structural Verilog: 2 circuits, main circuit main
module main (
  input  Door_Closed,
  input  [3:0] Original_Password,
  input  X3,
  input  X2,
  input  X1,
  input  X0,
  input  Clock_to_comparator_output_register,
  input  Change_Password,
  input  ENTER_Button,
  input  Comparator_output,
  input  G1,
  input  VCC,
  input  Change_Password_2,
  input  negative_of_Alarm_output,
  input  Factory_Reset,
  input  GND,
  input  Output_from_comparator_register,
  output locked,
  output unlocked
);

  wire and_1_out, and_2_out, and_3_out, and_4_out, clock_1_out, controlled_buffer_1_out, decoder_1_out1,
       decoder_1_out3, Factory_Reset_out, LED_Display_Ckt_a, LED_Display_Ckt_b, LED_Display_Ckt_d,
       LED_Display_Ckt_e, LED_Display_Ckt_f, LED_Display_Ckt_g, n7404_1_p2, n7404_1_p3, n7404_1_p4,
       n7404_1_p6, n7408_1_p3, n7432_1_p1, n7432_1_p7, n7432_1_p11, n7474_1_p3, n74139_1_p1, n74139_1_p2,
       not_1_out, not_2_out, not_3_out, not_4_out, not_5_out, not_6_out, or_1_out, or_2_out, or_3_out,
       or_4_out, or_5_out, register_1_q, register_2_q, Unlock_Button__inside_the_car_out;
  wire [1:0] counter_3_q, not_7_out;
  wire [2:1] and_5_out;
  wire [3:0] counter_1_q, counter_2_q, multiplexer_1_out, Password_2_q, Password_q;

  Button ENTER (.out(not_7_out[1]));
  not not_1 (not_1_out, counter_2_q[2]);
  Register #(.width(4)) Password (
    .D({X3, X2, X1, X0}), .en(not_1_out), .Q(Password_q), .clk(not_7_out[1]));  // open: clr
  or or_1 (or_1_out, Change_Password, not_2_out);
  Register #(.width(1)) register_1 (
    .D(Change_Password), .Q(register_1_q), .clk(and_1_out), .clr(Factory_Reset_out));  // open: en
  and and_1 (and_1_out, Change_Password, not_3_out, register_2_q);
  Comparator #(.width(4), .mode("unsigned")) comparator_1 (
    .a(Password_q), .b(Password_2_q), .eq(and_5_out[2]));  // open: gt, lt
  Register #(.width(4)) Password_2 (.D(multiplexer_1_out), .Q(Password_2_q), .clk(or_2_out));  // open: en, clr
  Multiplexer #(.width(4)) multiplexer_1 (
    .in0(Original_Password), .in1({X3, X2, X1, X0}), .out(multiplexer_1_out), .sel(register_1_q),
    .en(or_1_out));
  or or_2 (or_2_out, not_7_out[1], Factory_Reset_out);
  not not_2 (not_2_out, register_1_q);
  not not_3 (not_3_out, Factory_Reset_out);
  and and_2 (and_2_out, and_5_out[2], not_1_out);
  Register #(.width(1)) register_2 (
    .D(and_5_out[2]), .en(Change_Password), .Q(register_2_q), .clk(and_3_out), .clr(or_3_out));
  or or_3 (or_3_out, not_4_out, Factory_Reset_out);
  not not_4 (not_4_out, Change_Password);
  and and_3 (and_3_out, and_5_out[2], not_7_out[1]);
  Clock clock_1 (.out(clock_1_out));
  and and_4 (and_4_out, clock_1_out, Door_Closed, and_5_out[2]);
  not not_5 (not_5_out, Door_Closed);
  not not_6 (not_6_out, and_5_out[2]);
  assign controlled_buffer_1_out = decoder_1_out3 ? not_6_out : 1'bz;  // Controlled_Buffer controlled_buffer_1
  or or_4 (or_4_out, and_2_out, Factory_Reset_out);
  Decoder #(.select(2)) decoder_1 (
    .out1(decoder_1_out1), .out3(decoder_1_out3), .sel(not_7_out));  // open: out0, out2, en
  Counter #(.width(4), .max('hf), .ongoal("stay")) counter_1 (
    .count(1'b1), .Q(counter_1_q), .clk(and_4_out), .clr(or_5_out));  // open: load, D, carry
  or or_5 (or_5_out, Factory_Reset_out, not_5_out, Unlock_Button__inside_the_car_out);
  Counter #(.width(4), .max('hf)) counter_2 (
    .count(controlled_buffer_1_out), .Q(counter_2_q), .clk(decoder_1_out1), .clr(or_4_out));  // open: load, D, carry
  and and_5 (and_5_out[1], counter_1_q[0], counter_1_q[1], counter_1_q[2], counter_1_q[3]);
  not not_7 (not_7_out[0], counter_2_q[2]);
  Counter #(.width(2), .max('h3)) counter_3 (
    .Q(counter_3_q), .clk(Factory_Reset_out), .clr(counter_3_q[1]));  // open: load, D, count, carry
  Multiplexer #(.select(3)) multiplexer_2 (
    .in0(1'b1), .in1(1'b0), .in2(1'b1), .in3(1'b0), .in4(counter_2_q[2]), .in5(1'b0), .in6(1'b1), .in7(1'b0),
    .out(locked), .sel({and_5_out, counter_3_q[1]}));  // open: en
  not not_8 (unlocked, locked);
  LED Alarm (.in(counter_2_q[2]));
  LED_Display LED_Display_Ckt (
    .Input(counter_2_q[2:0]), .a(LED_Display_Ckt_a), .b(LED_Display_Ckt_b), .d(LED_Display_Ckt_d),
    .e(LED_Display_Ckt_e), .f(LED_Display_Ckt_f), .g(LED_Display_Ckt_g));
  Button Unlock_Button__inside_the_car (.out(Unlock_Button__inside_the_car_out));
  Button u_Factory_Reset (.out(Factory_Reset_out));
  _7_Segment_Display u_7_segment_display_1 (
    .g(LED_Display_Ckt_g), .f(LED_Display_Ckt_a), .a(LED_Display_Ckt_b), .b(1'b1), .e(LED_Display_Ckt_f),
    .d(LED_Display_Ckt_e), .c(LED_Display_Ckt_d));  // open: dp
  // _7404 7404_1: pin names not known; wires that end beside it: Factory_Reset, n7404_1_p2, n7404_1_p3, n7404_1_p4, Change_Password_2, n7404_1_p6
  // _7474 7474_1: pin names not known; wires that end beside it: Factory_Reset, Change_Password_2, n7474_1_p3, n7404_1_p3
  // _7432 7432_1: pin names not known; wires that end beside it: n7432_1_p1, Change_Password_2, n7404_1_p4, n7432_1_p1, ENTER_Button, Factory_Reset, n7432_1_p7, n7432_1_p7, Factory_Reset, n7404_1_p6, n7432_1_p11, n7432_1_p11
  // _7408 7408_1: pin names not known; wires that end beside it: Change_Password_2, n7404_1_p2, n7408_1_p3, n7408_1_p3, Output_from_comparator_register, n7474_1_p3, Comparator_output, ENTER_Button, Clock_to_comparator_output_register
  // NOT_Gate not_9 is placed but not wired
  // _74139 74139_1: pin names not known; wires that end beside it: n74139_1_p1, n74139_1_p2, G1, negative_of_Alarm_output, ENTER_Button, n74139_1_p2, n74139_1_p1, GND, VCC

  // Notes on the sheet:
  //   This can be used to reset if user takes it to repair center
  //   To async CLEAR of FF
  //   To Wrong attempts counter
  //   To tri state buffer
endmodule

// LED CKT
module LED_Display (
  input  [2:0] Input,
  output a,
  output b,
  output d,
  output e,
  output f,
  output g
);

  wire not_1_out;

  not not_1 (not_1_out, Input[0]);
  Multiplexer #(.select(2)) multiplexer_1 (
    .in0(not_1_out), .in1(1'b0), .in2(1'b1), .in3(1'b1), .out(a), .sel(Input[2:1]));  // open: en
  Multiplexer #(.select(2)) multiplexer_2 (
    .in0(Input[0]), .in1(not_1_out), .in2(not_1_out), .in3(1'b0), .out(b), .sel(Input[2:1]));  // open: en
  Multiplexer #(.select(2)) multiplexer_3 (
    .in0(1'b1), .in1(Input[0]), .in2(1'b1), .in3(1'b1), .out(d), .sel(Input[2:1]));  // open: en
  Multiplexer #(.select(2)) multiplexer_4 (
    .in0(Input[0]), .in1(not_1_out), .in2(not_1_out), .in3(1'b0), .out(e), .sel(Input[2:1]));  // open: en
  Multiplexer #(.select(2)) multiplexer_5 (
    .in0(1'b0), .in1(not_1_out), .in2(not_1_out), .in3(1'b0), .out(f), .sel(Input[2:1]));  // open: en
  Multiplexer #(.select(2)) multiplexer_6 (
    .in0(1'b1), .in1(not_1_out), .in2(Input[0]), .in3(1'b1), .out(g), .sel(Input[2:1]));  // open: en
endmodule
