// Logisim project T Flip-Flop.circ as structural Verilog: 3 circuits, main circuit main
module main (
  input  T,
  output Q
);

  wire CLK_out;

  Clock CLK (.out(CLK_out));
  T_FF t_ff_1 (.CLK(CLK_out), .T(T), .Q(Q));  // open: Q_prime
endmodule

module SR_Latch (
  input  S,
  input  R,
  output Q,
  output Q_prime
);

  nor nor_1 (Q, S, Q_prime);
  nor nor_2 (Q_prime, Q, R);
endmodule

module T_FF (
  input  CLK,
  input  T,
  output Q,
  output Q_prime
);

  wire and_1_out, and_2_out, and_3_out, and_4_out, not_1_out, not_2_out, sr_latch_2_q, sr_latch_2_q_prime;

  not not_1 (not_1_out, CLK);
  not not_2 (not_2_out, T);
  and and_1 (and_1_out, not_1_out, sr_latch_2_q);
  and and_2 (and_2_out, not_1_out, sr_latch_2_q_prime);
  and and_3 (and_3_out, T, CLK);
  and and_4 (and_4_out, not_2_out, CLK);
  SR_Latch sr_latch_1 (.S(and_1_out), .R(and_2_out), .Q(Q), .Q_prime(Q_prime));
  SR_Latch sr_latch_2 (.S(and_3_out), .R(and_4_out), .Q(sr_latch_2_q), .Q_prime(sr_latch_2_q_prime));
endmodule
